# Fritzing sketch esp32 (saved by Fritzing 0.9.3b)
breadboards: 1

parts:
  Componente1 = Adafruit APDS-9960 [part_number="Adafruit #3595"]
  MH-ET_LIVE_ESP32_DEVKIT1 = MH-ET LIVE ESP32 DEVKIT 38 pins

nets:
  VIN: Componente1.VIN, MH-ET_LIVE_ESP32_DEVKIT1.5V
  N1: Componente1.GND, MH-ET_LIVE_ESP32_DEVKIT1.CMD
  N2: Componente1.SCL, MH-ET_LIVE_ESP32_DEVKIT1.IO22

custom parts:
  Adafruit APDS-9960: The APDS9960 from Avago Technologies has an integrated IR LED and driver, along with four directional photodiodes that sense reflected IR energy from the LED. It's proximity detection feature allows it to measure the distance an object is from the front of the sensor (up to a few centimeters) with 8 bit resolution. Since there are four IR sensors, you can measure the changes in light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
  MH-ET LIVE ESP32 DEVKIT 38 pins: http://mh.nodebb.com/topic/2/mh-et-live-esp32-devkit
