# Fritzing sketch raspberry (saved by Fritzing 0.9.3b)
breadboards: 1

parts:
  Componente1 = Adafruit APDS-9960 [part_number="Adafruit #3595"]
  Mod1 = Raspberry Pi Pico

nets:
  N1: Componente1.GND, Mod1.pin_38, Mod1.pin_40, Mod1.pin_42
  N2: Componente1.SCL, Mod1.pin_7
  N3: Componente1.SDA, Mod1.pin_6

custom parts:
  Adafruit APDS-9960: The APDS9960 from Avago Technologies has an integrated IR LED and driver, along with four directional photodiodes that sense reflected IR energy from the LED. It's proximity detection feature allows it to measure the distance an object is from the front of the sensor (up to a few centimeters) with 8 bit resolution. Since there are four IR sensors, you can measure the changes in light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
  Raspberry Pi Pico: Raspberry Pi Pico. Based around the RP2040 microcontroller the Pico is a low cost microcontroller device bringing Raspberry Pi quality, cost, and easy of use to the microcontroller space. Jan 2021, Split part in to two versions: tht (this one) and SMD. This one will drill holes for a .1 in header in pcb to allow plugging in the module as well as providing pads to solder the module to the top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
