# Fritzing sketch esp32 (saved by Fritzing 0.9.3b)
breadboards: 1

parts:
  MH-ET_LIVE_ESP32_DEVKIT1 = MH-ET LIVE ESP32 DEVKIT 38 pins
  MPU-1 = Adafruit MPU6050

nets:
  N1: MH-ET_LIVE_ESP32_DEVKIT1.CMD, MPU-1.GND
  5V: MH-ET_LIVE_ESP32_DEVKIT1.5V, MPU-1.VCC
  N2: MH-ET_LIVE_ESP32_DEVKIT1.IO22, MPU-1.SDA
  N3: MH-ET_LIVE_ESP32_DEVKIT1.IO21, MPU-1.SCL

custom parts:
  MH-ET LIVE ESP32 DEVKIT 38 pins: http://mh.nodebb.com/topic/2/mh-et-live-esp32-devkit
  Adafruit MPU6050: The MPU-6050 is a popular six axis accelerometer and gyroscope (gyro) that has all the info you need on how things are shakin' and spinnin' . With six axes of sensing and 16-bit measurements, you'll have everything you need to give your robot friend an inner ear. This combination of gyroscopes and accelerometers is commonly referred to as an Inertial Measurement Unit or IMU. Not so long ago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
